// Logisim project main.circ as structural Verilog: 7 circuits, main circuit main
module main (
  input  Power
);

  wire clk, cpu_1_ram_cs, cpu_1_ram_r_w, rst;
  wire [15:0] cpu_1_or_output, cpu_1_ram_address, cpu_1_ram_data_out, ram_1_data_out;

  Clock Clock (.out(clk));
  Button Reset (.out(rst));
  cpu cpu_1 (
    .power_on(Power), .clock(clk), .reset(rst), .RAM_data_in(ram_1_data_out), .RAM_cs(cpu_1_ram_cs),
    .RAM_r_w(cpu_1_ram_r_w), .RAM_data_out(cpu_1_ram_data_out), .RAM_address(cpu_1_ram_address),
    .OR_output(cpu_1_or_output));  // open: Output_trigger
  Hex_Digit_Display hex_digit_display_1 (.value(cpu_1_or_output[15:12]));  // open: dp
  Hex_Digit_Display hex_digit_display_2 (.value(cpu_1_or_output[11:8]));  // open: dp
  Hex_Digit_Display hex_digit_display_3 (.value(cpu_1_or_output[7:4]));  // open: dp
  Hex_Digit_Display hex_digit_display_4 (.value(cpu_1_or_output[3:0]));  // open: dp
  ram ram_1 (
    .Address(cpu_1_ram_address), .Data_in(cpu_1_ram_data_out), .Chip_Select(cpu_1_ram_cs),
    .Read__0____write__1(cpu_1_ram_r_w), .Data_out(ram_1_data_out), .Clear(rst));

  // Other names for the same wires on the sheet: pwr = Power
endmodule

module ram (
  input  [15:0] Address,
  input  [15:0] Data_in,
  input  Clear,
  input  Chip_Select,
  input  Read__0____write__1,
  output [15:0] Data_out
);

  wire and_1_out, not_1_out, not_2_out;
  wire [15:0] ram_1_data;

  not not_1 (not_1_out, Read__0____write__1);
  RAM #(.addrWidth(16), .dataWidth(16), .bus("separate")) ram_1 (
    .addr(Address), .din(Data_in), .data(ram_1_data), .str(Read__0____write__1), .sel(Chip_Select),
    .clk(not_2_out), .ld(not_1_out), .clr(Clear));
  not not_2 (not_2_out, not_1_out);
  and and_1 (and_1_out, Chip_Select, not_1_out);
  assign Data_out = and_1_out ? ram_1_data : 16'bz;  // Controlled_Buffer controlled_buffer_1

  // Notes on the sheet:
  //   128KB RAM module
endmodule

module cpu (
  input  power_on,
  input  clock,
  input  reset,
  input  [15:0] RAM_data_in,
  output RAM_cs,
  output RAM_r_w,
  output Output_trigger,
  output [15:0] RAM_data_out,
  output [15:0] RAM_address,
  output [15:0] OR_output
);

  wire a_ie, b_ie, bkp_ie, bkp_oe, cu_1_mar_ie, cu_1_r7_ie, cu_1_r7_oe, cu_1_ram_cs, cu_1_ram_r_w, cu_en,
       flg_ie, hlt, ir_ie, jr_ie, jr_oe, mar_ie, nb, not_1_out, o_ie, o_oe, r0_ie, r0_oe, r1_ie, r1_oe,
       r2_ie, r2_oe, r3_ie, r3_oe, r4_ie, r4_oe, r5_ie, r5_oe, r6_ie, r6_oe, r7_ie, r7_oe, tmp_ie, tmp_oe;
  wire [2:0] counter_1_q, op_code;
  wire [3:0] alu_1_v_c_z_s, flg_out;
  wire [9:4] multiplexer_1_out;
  wire [15:0] A_output, adder_1_out, alu_1_output, B_output, instr;

  Counter #(.width(3), .max('h5)) counter_1 (
    .count(not_1_out), .Q(counter_1_q), .clk(clock), .clr(reset));  // open: load, D, carry
  not not_1 (not_1_out, hlt);
  Multiplexer #(.select(3), .width(11), .disabled(0)) multiplexer_1 (
    .in0(11'h200), .in1(11'h2), .in2(11'hc8), .in3(11'h410), .in4(11'h104), .in5(11'h41),
    .out({ir_ie, multiplexer_1_out, tmp_ie, tmp_oe, bkp_ie, bkp_oe}), .sel(counter_1_q), .en(power_on));  // open: in6, in7
  reg_16b R0 (
    .Data(RAM_data_in), .Input_Enable(r0_ie), .Clock(clock), .Output(RAM_data_in), .Output_Enable(r0_oe),
    .Clear(reset));
  reg_16b R1 (
    .Data(RAM_data_in), .Input_Enable(r1_ie), .Clock(clock), .Output(RAM_data_in), .Output_Enable(r1_oe),
    .Clear(reset));
  reg_16b R2 (
    .Data(RAM_data_in), .Input_Enable(r2_ie), .Clock(clock), .Output(RAM_data_in), .Output_Enable(r2_oe),
    .Clear(reset));
  reg_16b R3 (
    .Data(RAM_data_in), .Input_Enable(r3_ie), .Clock(clock), .Output(RAM_data_in), .Output_Enable(r3_oe),
    .Clear(reset));
  reg_16b R4 (
    .Data(RAM_data_in), .Input_Enable(r4_ie), .Clock(clock), .Output(RAM_data_in), .Output_Enable(r4_oe),
    .Clear(reset));
  reg_16b SP__R5 (
    .Data(RAM_data_in), .Input_Enable(r5_ie), .Clock(clock), .Output(RAM_data_in), .Output_Enable(r5_oe),
    .Clear(reset));
  reg_16b LR__R6 (
    .Data(RAM_data_in), .Input_Enable(r6_ie), .Clock(clock), .Output(RAM_data_in), .Output_Enable(r6_oe),
    .Clear(reset));
  reg_16b PC__R7 (
    .Data(RAM_data_in), .Input_Enable(r7_ie), .Clock(clock), .Output(RAM_data_in), .Output_Enable(r7_oe),
    .Clear(reset));
  reg_16b JR (
    .Data(RAM_data_in), .Input_Enable(jr_ie), .Clock(clock), .Output(RAM_data_in), .Output_Enable(jr_oe),
    .Clear(reset));
  and and_1 (cu_en, multiplexer_1_out[9], power_on);
  or or_1 (r7_ie, multiplexer_1_out[8], cu_1_r7_ie);
  or or_2 (RAM_cs, multiplexer_1_out[4], cu_1_ram_cs);
  or or_3 (r7_oe, multiplexer_1_out[7], cu_1_r7_oe);
  or or_4 (mar_ie, multiplexer_1_out[6], cu_1_mar_ie);
  or or_5 (RAM_r_w, multiplexer_1_out[5], cu_1_ram_r_w);
  reg_16b IR (
    .Data(RAM_data_in), .Input_Enable(ir_ie), .Clock(clock), .Output(instr), .Output_Enable(power_on),
    .Clear(reset));
  reg_16b A (
    .Data(RAM_data_in), .Input_Enable(a_ie), .Clock(clock), .Output(A_output), .Output_Enable(power_on),
    .Clear(reset));
  reg_16b OUT (
    .Data(alu_1_output), .Input_Enable(o_ie), .Clock(clock), .Output(RAM_data_in), .Output_Enable(o_oe),
    .Clear(reset));
  reg_16b MAR (
    .Data(RAM_data_in), .Input_Enable(mar_ie), .Clock(clock), .Output(RAM_address), .Output_Enable(power_on),
    .Clear(reset));
  reg_16b OR_6 (
    .Data(RAM_data_in), .Input_Enable(Output_trigger), .Clock(clock), .Output(OR_output),
    .Output_Enable(power_on), .Clear(reset));
  alu alu_1 (
    .Input_A(A_output), .Input_B(B_output), .nB(nb), .Output(alu_1_output), .Op_code(op_code),
    .V_C_Z_S(alu_1_v_c_z_s));
  reg_16b TMP (
    .Data(adder_1_out), .Input_Enable(tmp_ie), .Clock(clock), .Output(RAM_data_in), .Output_Enable(tmp_oe),
    .Clear(reset));
  Adder #(.width(16)) adder_1 (.a(RAM_data_in), .b({16{1'b0}}), .out(adder_1_out), .cin(power_on));  // open: cout
  reg_16b B (
    .Data(RAM_data_in), .Input_Enable(b_ie), .Clock(clock), .Output(B_output), .Output_Enable(power_on),
    .Clear(reset));
  reg_4b FLAGS (
    .Data(alu_1_v_c_z_s), .Input_Enable(flg_ie), .Clock(clock), .Output(flg_out), .Output_Enable(power_on),
    .Clear(reset));
  reg_16b BKP (
    .Data(RAM_address), .Input_Enable(bkp_ie), .Clock(clock), .Output(RAM_data_in), .Output_Enable(bkp_oe),
    .Clear(reset));
  cu cu_1 (
    .Instruction(instr), .Flags(flg_out), .R0_IE(r0_ie), .R0_OE(r0_oe), .R1_IE(r1_ie), .R1_OE(r1_oe),
    .R2_IE(r2_ie), .R2_OE(r2_oe), .R3_IE(r3_ie), .R3_OE(r3_oe), .R4_IE(r4_ie), .R4_OE(r4_oe), .R5_IE(r5_ie),
    .R5_OE(r5_oe), .R6_IE(r6_ie), .R6_OE(r6_oe), .R7_IE(cu_1_r7_ie), .R7_OE(cu_1_r7_oe), .A_IE(a_ie),
    .B_IE(b_ie), .nB(nb), .OUT_IE(o_ie), .OUT_OE(o_oe), .OP_CODE(op_code), .FLG_IE(flg_ie),
    .BUS_output(RAM_data_in), .MAR_IE(cu_1_mar_ie), .RAM_R_W(cu_1_ram_r_w), .RAM_CS(cu_1_ram_cs),
    .OR_IE(Output_trigger), .HLT(hlt), .Enable(cu_en), .JR_IE(jr_ie), .JR_OE(jr_oe));

  assign RAM_data_out = RAM_data_in;

  // Other names for the same wires on the sheet: bus[15:0] = RAM_data_in; clear = reset; clk = clock;
  //   or_ie = Output_trigger; OR_out[15:0] = OR_output; pwr = power_on; RAM_addr[15:0] = RAM_address

  // Notes on the sheet:
  //   Fetch-decode-execute cycle
  //   16bit CPU
  //   Control Unit
endmodule

module cu (
  input  [15:0] Instruction,
  input  [3:0] Flags,
  input  Enable,
  output R0_IE,
  output R0_OE,
  output R1_IE,
  output R1_OE,
  output R2_IE,
  output R2_OE,
  output R3_IE,
  output R3_OE,
  output R4_IE,
  output R4_OE,
  output R5_IE,
  output R5_OE,
  output R6_IE,
  output R6_OE,
  output R7_IE,
  output R7_OE,
  output A_IE,
  output B_IE,
  output nB,
  output OUT_IE,
  output OUT_OE,
  output [2:0] OP_CODE,
  output FLG_IE,
  output [15:0] BUS_output,
  output MAR_IE,
  output RAM_R_W,
  output RAM_CS,
  output OR_IE,
  output HLT,
  output JR_IE,
  output JR_OE
);

  wire and_1_out, and_2_out, cond, not_1_out, not_2_out, not_3_out, not_4_out, or_1_out, or_2_out, or_3_out,
       special_ctrl;
  wire [15:0] bus_out__jmp, bus_out__set, multiplexer_4_out;
  wire [30:11] to_mem;
  wire [31:0] bit_extender_2_out, cmd_01, multiplexer_2_out, multiplexer_5_out, multiplexer_6_out, \reg ;
  wire [31:3] cmd_10, from_mem;

  Decoder #(.select(4), .disabled(0), .enable("false")) decoder_1 (
    .out0(\reg [30]), .out1(\reg [28]), .out2(\reg [26]), .out3(\reg [24]), .out4(\reg [22]),
    .out5(\reg [20]), .out6(\reg [18]), .out7(\reg [16]), .out10(\reg [11]), .out13(\reg [0]),
    .sel(Instruction[8:5]));  // open: out8, out9, out11, out12, out14, out15
  Decoder #(.select(4), .disabled(0), .enable("false")) decoder_2 (
    .out0(\reg [31]), .out1(\reg [29]), .out2(\reg [27]), .out3(\reg [25]), .out4(\reg [23]),
    .out5(\reg [21]), .out6(\reg [19]), .out7(\reg [17]), .out8(\reg [15]), .out9(\reg [14]),
    .out11(\reg [6]), .out12(\reg [3]), .sel(Instruction[4:1]));  // open: out10, out13, out14, out15
  Multiplexer #(.width(32), .disabled(0), .enable("false")) multiplexer_1 (
    .in0({\reg [31:14], 2'b00, \reg [11], 4'b0000, \reg [6], 2'b00, \reg [3], 2'b00, \reg [0]}),
    .in1(multiplexer_2_out), .out(cmd_01), .sel(Instruction[9]));
  Multiplexer #(.width(32), .disabled(0), .enable("false")) multiplexer_2 (
    .in0({from_mem[31], 1'b0, from_mem[29], 1'b0, from_mem[27], 1'b0, from_mem[25], 1'b0, from_mem[23], 1'b0, from_mem[21], 1'b0, from_mem[19], 1'b0, from_mem[17], 1'b0, from_mem[15:14], {7{1'b0}}, from_mem[6], 2'b01, from_mem[3], 3'b000}),
    .in1({1'b0, to_mem[30], 1'b0, to_mem[28], 1'b0, to_mem[26], 1'b0, to_mem[24], 1'b0, to_mem[22], 1'b0, to_mem[20], 1'b0, to_mem[18], 1'b0, to_mem[16], 4'b0000, to_mem[11], 11'h30}),
    .out(multiplexer_2_out), .sel(Instruction[8]));
  Decoder #(.select(4), .disabled(0), .enable("false")) decoder_3 (
    .out0(cmd_10[31]), .out1(cmd_10[29]), .out2(cmd_10[27]), .out3(cmd_10[25]), .out4(cmd_10[23]),
    .out5(cmd_10[21]), .out6(cmd_10[19]), .out7(cmd_10[17]), .out8(cmd_10[15]), .out9(cmd_10[14]),
    .out11(cmd_10[6]), .out12(cmd_10[3]), .sel(Instruction[9:6]));  // open: out10, out13, out14, out15
  assign bus_out__set = {{10{1'b0}}, Instruction[5:0]};  // Bit_Extender bit_extender_1
  Decoder #(.select(4), .disabled(0), .enable("false")) decoder_4 (
    .out0(from_mem[31]), .out1(from_mem[29]), .out2(from_mem[27]), .out3(from_mem[25]), .out4(from_mem[23]),
    .out5(from_mem[21]), .out6(from_mem[19]), .out7(from_mem[17]), .out8(from_mem[15]), .out9(from_mem[14]),
    .out11(from_mem[6]), .out12(from_mem[3]), .sel(Instruction[7:4]));  // open: out10, out13, out14, out15
  or or_1 (or_1_out, Flags[0], Flags[1]);
  or or_2 (or_2_out, Flags[1], ~Flags[0]);  // OR_Gate
  not not_1 (not_1_out, Flags[1]);
  not not_2 (not_2_out, Flags[0]);
  Multiplexer #(.select(4), .disabled(0), .enable("false")) multiplexer_3 (
    .in0(1'b1), .in1(Flags[1]), .in2(not_1_out), .in3(Flags[0]), .in4(or_1_out), .in5(not_2_out),
    .in6(or_2_out), .in7(Flags[3]), .in8(not_3_out), .in9(Flags[2]), .in10(not_4_out), .out(cond),
    .sel(Instruction[13:10]));  // open: in11, in12, in13, in14, in15
  not not_3 (not_3_out, Flags[3]);
  not not_4 (not_4_out, Flags[2]);
  and and_1 (and_1_out, Instruction[15], ~Instruction[14]);  // AND_Gate
  or or_3 (or_3_out, ~special_ctrl, and_1_out);  // OR_Gate
  and and_2 (and_2_out, Enable, or_3_out);
  Multiplexer #(.width(16), .disabled(0)) multiplexer_4 (
    .in0(bus_out__jmp), .in1(bus_out__set), .out(multiplexer_4_out), .sel(special_ctrl), .en(Enable));
  Decoder #(.select(4), .disabled(0), .enable("false")) decoder_5 (
    .out0(to_mem[30]), .out1(to_mem[28]), .out2(to_mem[26]), .out3(to_mem[24]), .out4(to_mem[22]),
    .out5(to_mem[20]), .out6(to_mem[18]), .out7(to_mem[16]), .out10(to_mem[11]), .sel(Instruction[7:4]));  // open: out8, out9, out11, out12, out13, out14, out15
  Multiplexer #(.select(2), .width(32), .disabled(0)) multiplexer_5 (
    .in0({{29{1'b0}}, Instruction[9], 2'b00}), .in1(cmd_01),
    .in2({cmd_10[31], 1'b0, cmd_10[29], 1'b0, cmd_10[27], 1'b0, cmd_10[25], 1'b0, cmd_10[23], 1'b0, cmd_10[21], 1'b0, cmd_10[19], 1'b0, cmd_10[17], 1'b0, cmd_10[15:14], {7{1'b0}}, cmd_10[6], 2'b00, cmd_10[3], 3'b000}),
    .in3({{18{1'b0}}, Instruction[6], 2'b10, Instruction[9:7], Instruction[5], {7{1'b0}}}),
    .out(multiplexer_5_out), .sel(Instruction[15:14]), .en(Enable));
  assign bit_extender_2_out = {{31{cond}}, cond};  // Bit_Extender bit_extender_2
  assign BUS_output = and_2_out ? multiplexer_4_out : 16'bz;  // Controlled_Buffer controlled_buffer_1
  or or_4 (special_ctrl, ~Instruction[0], Instruction[15]);  // OR_Gate
  Multiplexer #(.width(32), .disabled(0)) multiplexer_6 (
    .in0(32'h2), .in1(multiplexer_5_out), .out(multiplexer_6_out), .sel(special_ctrl), .en(Enable));
  assign {R0_IE, R0_OE, R1_IE, R1_OE, R2_IE, R2_OE, R3_IE, R3_OE, R4_IE, R4_OE, R5_IE, R5_OE, R6_IE, R6_OE, R7_IE, R7_OE, A_IE, B_IE, nB, OUT_IE, OUT_OE, OP_CODE, FLG_IE, MAR_IE, RAM_R_W, RAM_CS, OR_IE, HLT, JR_IE, JR_OE} = multiplexer_6_out & bit_extender_2_out;  // AND_Gate and_3, 32 bits wide
  Adder #(.width(16)) adder_1 (
    .a({2'b00, Instruction[14:1]}), .b(16'h4000), .out(bus_out__jmp), .cin(1'b0));  // open: cout

  // Other names for the same wires on the sheet: cmd_11 (some bits) = {Instruction[6], Instruction[9:7], Instruction[5]};
  //   cmd_00[2] = Instruction[9]; instr[1:0] = Instruction[15:14]; S = Flags[0]; Z = Flags[1]; C = Flags[2];
  //   V = Flags[3]; special[1:0] = {Instruction[15], Instruction[0]}

  // Notes on the sheet:
  //   NOP & HLT commands
  //   EXC command
  //   MOV command
  //   MOV (reg to reg)
  //   Control Unit
  //   SET command
  //   MOV (mem to reg)
  //   Condition control
  //   CU outputs
  //   MOV (reg to mem)
  //   JMP command
endmodule

module alu (
  input  [15:0] Input_A,
  input  [15:0] Input_B,
  input  nB,
  input  [2:0] Op_code,
  output [15:0] Output,
  output [3:0] V_C_Z_S
);

  wire xnor_1_out, xor_2_out;
  wire [15:0] adder_1_out, and_1_out, B, not_1_out, not_2_out, or_1_out, shifter_1_out, shifter_2_out,
       shifter_3_out, xor_1_out;

  Multiplexer #(.width(16), .disabled(0), .enable("false")) multiplexer_1 (
    .in0(Input_B), .in1(not_1_out), .out(B), .sel(nB));
  assign not_1_out = ~Input_B;  // NOT_Gate not_1, 16 bits wide
  Adder #(.width(16)) adder_1 (.a(Input_A), .b(B), .out(adder_1_out), .cin(nB), .cout(V_C_Z_S[2]));
  assign and_1_out = Input_A & B;  // AND_Gate and_1, 16 bits wide
  assign or_1_out = Input_A | B;  // OR_Gate or_1, 16 bits wide
  assign xor_1_out = Input_A ^ B;  // XOR_Gate xor_1, 16 bits wide
  assign not_2_out = ~Input_A;  // NOT_Gate not_2, 16 bits wide
  Shifter #(.width(16)) shifter_1 (.in(Input_A), .\dist (B[3:0]), .out(shifter_1_out));
  Shifter #(.width(16), .shift("lr")) shifter_2 (.in(Input_A), .\dist (B[3:0]), .out(shifter_2_out));
  Shifter #(.width(16), .shift("ar")) shifter_3 (.in(Input_A), .\dist (B[3:0]), .out(shifter_3_out));
  Multiplexer #(.select(3), .width(16), .disabled(0), .enable("false")) multiplexer_2 (
    .in0(adder_1_out), .in1(and_1_out), .in2(or_1_out), .in3(xor_1_out), .in4(not_2_out),
    .in5(shifter_1_out), .in6(shifter_2_out), .in7(shifter_3_out), .out(Output), .sel(Op_code));
  xor xor_2 (xor_2_out, Input_A[15], Output[15]);
  xnor xnor_1 (xnor_1_out, Input_A[15], B[15]);
  and and_2 (V_C_Z_S[3], xnor_1_out, xor_2_out);
  Comparator #(.width(16)) comparator_1 (.a(Output), .b({16{1'b0}}), .eq(V_C_Z_S[1]));  // open: gt, lt

  assign V_C_Z_S[0] = Output[15];

  // Other names for the same wires on the sheet: A[15:0] = Input_A; O[15:0] = Output; c_out = V_C_Z_S[2]

  // Notes on the sheet:
  //   16bit ALU
  //   Flags control
endmodule

module reg_16b (
  input  [15:0] Data,
  input  Input_Enable,
  input  Output_Enable,
  input  Clock,
  input  Clear,
  output [15:0] Output
);

  wire and_1_out;
  wire [15:0] register_1_q;

  Register #(.width(16)) register_1 (.D(Data), .en(and_1_out), .Q(register_1_q), .clk(and_1_out), .clr(Clear));
  and and_1 (and_1_out, Input_Enable, ~Clock);  // AND_Gate
  assign Output = Output_Enable ? register_1_q : 16'bz;  // Controlled_Buffer controlled_buffer_1

  // Notes on the sheet:
  //   General purpose 16bit register
endmodule

module reg_4b (
  input  [3:0] Data,
  input  Input_Enable,
  input  Output_Enable,
  input  Clock,
  input  Clear,
  output [3:0] Output
);

  wire and_1_out;
  wire [3:0] register_1_q;

  Register #(.width(4)) register_1 (.D(Data), .en(and_1_out), .Q(register_1_q), .clk(and_1_out), .clr(Clear));
  and and_1 (and_1_out, Input_Enable, ~Clock);  // AND_Gate
  assign Output = Output_Enable ? register_1_q : 4'bz;  // Controlled_Buffer controlled_buffer_1

  // Notes on the sheet:
  //   General purpose 4bit register
endmodule
